# Fritzing sketch Untitled Sketch (saved by Fritzing 0.9.3b)
breadboards: 1

parts:
  Part1 = LCD1602-I2C
  Part2 = Arduino Uno (Rev3)
  S1 = Pushbutton [package="[SMD]"]
  S2 = Pushbutton [package="[SMD]"]

nets:
  GND: Part1.GND, Part2.GND, S1.Pin_1, S1.Pin_2, S2.Pin_1, S2.Pin_2
  VCC: Part1.VCC, Part2.5V
  N1: Part1.SDA, Part2.A4/SDA
  N2: Part1.SCL, Part2.A5/SCL
  N3: Part2.D10_PWM/SS, S2.Pin_3, S2.Pin_4
  N4: Part2.D11_PWM/MOSI, S1.Pin_3, S1.Pin_4

custom parts:
  LCD1602-I2C: A standard character display, usually with 2x16 characters. Comes in many colors with LCM1602 IIC attached.

// code stored in the sketch: Untitled.ino
#include <Wire.h>
#include <LiquidCrystal_I2C.h>
LiquidCrystal_I2C lcd(0x27,16,2);
const int  tipkalo1 = 11;
const int  tipkalo2 = 10;



void setup() {  
  lcd.init();
  // put your setup code here, to run once:
pinMode(tipkalo1, INPUT_PULLUP);
pinMode(tipkalo2, INPUT_PULLUP);
}


void loop() {
  // put your main code here, to run repeatedly:
if (digitalRead(tipkalo1) == LOW){
  lcd.backlight();
  }
else if (digitalRead(tipkalo2)==LOW){
lcd.noBacklight();
}


  while (digitalRead(tipkalo2)==LOW) {
    if (digitalRead(tipkalo1) == LOW){
  lcd.begin(16,2);
  lcd.setCursor(0,0);
  lcd.print("D");
  lcd.print("a");
  lcd.print("v");
  lcd.print("o");
  lcd.print("r");


  }
}
}
